// Logisim project EXERCÍCIO 001.circ as structural Verilog: 1 circuit, main circuit main
module main (
  input  A,
  input  A_2,
  input  B,
  input  A_3,
  input  B_2,
  input  C,
  input  B_3,
  input  C_2,
  input  C_3,
  input  C_4,
  input  A_4,
  input  D,
  input  B_4,
  input  B_5,
  input  D_2,
  input  A_5,
  input  B_6,
  input  C_5,
  input  D_3,
  input  in_20,
  input  A_6,
  input  in_22,
  input  in_23,
  input  B_7,
  input  C_6,
  input  in_26,
  input  D_4,
  input  in_28,
  input  E,
  input  in_30,
  input  in_31,
  input  in_32,
  output out_33,
  output out_34,
  output out_35,
  output out_36,
  output out_37
);

  wire and_3_out, and_4_out, and_5_out, and_6_out, and_7_out, and_9_out, and_10_out, nand_1_out, nand_2_out,
       nand_3_out, nor_1_out, or_1_out, or_2_out, or_3_out, or_4_out, or_5_out, or_6_out, or_8_out;

  or or_1 (or_1_out, A_2, B_2);
  or or_2 (or_2_out, B_4, D_2);
  nor nor_1 (nor_1_out, ~A_5, ~B_6);  // NOR_Gate
  nand nand_1 (nand_1_out, ~C_5, D_3);  // NAND_Gate
  and and_1 (out_35, or_1_out, C_3, or_2_out);
  or or_3 (or_3_out, nor_1_out, nand_1_out);
  and and_2 (out_36, or_3_out, ~in_20);  // AND_Gate
  nand nand_2 (nand_2_out, ~A_6, B_7);  // NAND_Gate
  nand nand_3 (nand_3_out, C_6, ~D_4);  // NAND_Gate
  and and_3 (and_3_out, A_6, ~D_4, ~E);  // AND_Gate
  and and_4 (and_4_out, C_6, D_4, E);
  or or_4 (or_4_out, nand_2_out, nand_3_out);
  or or_5 (or_5_out, and_3_out, and_4_out);
  and and_5 (and_5_out, A, B, C);
  or or_6 (or_6_out, A_4, B_5);
  and and_6 (and_6_out, or_4_out, E);
  and and_7 (and_7_out, C_2, or_6_out);
  or or_7 (out_33, and_5_out, and_7_out);
  or or_8 (or_8_out, and_6_out, or_5_out);
  and and_8 (out_37, or_8_out, ~A_6);  // AND_Gate
  and and_9 (and_9_out, ~A_3, ~B_3);  // AND_Gate
  and and_10 (and_10_out, ~C_4, ~D);  // AND_Gate
  nor nor_2 (out_34, and_9_out, and_10_out);
  // NOT_Gate not_1 is placed but not wired

  assign in_22 = A_6;
  assign in_23 = A_6;
  assign in_26 = C_6;
  assign in_28 = D_4;
  assign in_30 = E;
  assign in_31 = D_4;
  assign in_32 = E;

  // Notes on the sheet:
  //   A)
  //   D)
  //   E)
  //   B)
  //   C)
endmodule
