// Logisim project EXERCÍCIO 002.circ as structural Verilog: 1 circuit, main circuit main
// B
module main (
  input  A,
  input  A_2,
  input  in_3,
  input  in_4,
  input  B,
  input  A_3,
  input  C,
  input  in_8,
  input  B_2,
  input  D,
  input  A_4,
  input  A_5,
  input  B_3,
  input  B_4,
  input  C_2,
  input  D_2,
  input  B_5,
  input  B_6,
  input  D_3,
  input  A_6,
  input  A_7,
  input  C_3,
  input  B_7,
  input  C_4,
  output out_25,
  output out_26,
  output out_27,
  output out_28
);

  wire and_1_out, and_2_out, and_4_out, and_5_out, and_6_out, and_8_out, or_1_out, or_2_out, or_3_out,
       or_4_out, or_6_out, or_7_out, or_8_out, or_9_out;

  or or_1 (or_1_out, A_5, B_4);
  or or_2 (or_2_out, A_6, C_3);
  or or_3 (or_3_out, A_2, B);
  or or_4 (or_4_out, C, D);
  and and_1 (and_1_out, or_1_out, D_2);
  buf and_2 (and_2_out, or_2_out);  // AND_Gate
  and and_3 (out_27, and_1_out, and_2_out);
  or or_5 (out_26, or_3_out, or_4_out);
  or or_6 (or_6_out, A, in_3, in_4);
  or or_7 (or_7_out, A_3, in_8, B_2);
  or or_8 (or_8_out, A_4, B_3);
  and and_4 (and_4_out, B_5, D_3);
  and and_5 (and_5_out, B_7, C_4);
  and and_6 (and_6_out, or_8_out, C_2);
  or or_9 (or_9_out, and_4_out, A_7);
  and and_7 (out_25, or_6_out, or_7_out);
  and and_8 (and_8_out, or_9_out, and_5_out);
  or or_10 (out_28, and_6_out, and_8_out);

  // Notes on the sheet:
  //   B
  //   C
  //   D
endmodule
