// Logisim project EXERCÍCIO 01.circ as structural Verilog: 1 circuit, main circuit main
// B
module main (
  input  A,
  input  B,
  input  C,
  input  D,
  input  A_2,
  input  in_6,
  input  in_7,
  input  A_3,
  input  in_9,
  input  B_2,
  input  A_4,
  input  B_3,
  input  D_2,
  input  B_4,
  input  A_5,
  input  C_2,
  input  A_6,
  input  C_3,
  input  B_5,
  input  B_6,
  input  C_4,
  output out_22,
  output out_23,
  output out_24
);

  wire and_1_out, or_1_out, or_2_out, or_3_out, or_4_out, or_5_out, or_6_out, or_7_out;

  or or_1 (or_1_out, A_5, C_2);
  or or_2 (or_2_out, A, B);
  or or_3 (or_3_out, C, D);
  or or_4 (or_4_out, A_2, in_6, in_7);
  or or_5 (or_5_out, A_3, in_9, B_2);
  or or_6 (or_6_out, A_4, B_3);
  or or_7 (or_7_out, A_6, B_5);
  and and_1 (and_1_out, B_6, C_4);
  and and_2 (out_23, or_4_out, or_5_out);
  and and_3 (out_24, D_2, B_3, B_4);
  // AND_Gate and_4 has open pins: in0=C_3, in1=and_1_out, out=open
  or or_8 (out_22, or_2_out, or_3_out);
  // AND_Gate and_5 is placed but not wired

  // Notes on the sheet:
  //   B
  //   C
  //   D
  //   B
  //   D
endmodule
