// Logisim project EXERCÍCIOS.circ as structural Verilog: 1 circuit, main circuit main
module main (
  input  in_1,
  input  in_2,
  input  in_3,
  input  in_4,
  input  in_5,
  input  [1:0] in_6,
  input  [1:0] in_7,
  input  in_8,
  input  in_9,
  input  in_10,
  input  in_11,
  input  in_12,
  input  in_13,
  input  [1:0] in_14,
  input  [1:0] in_15,
  input  in_16,
  input  in_17,
  input  in_18,
  input  in_19,
  input  in_20,
  input  [1:0] in_21,
  input  in_22,
  input  in_23,
  input  in_24,
  input  in_25,
  input  in_26,
  input  [1:0] in_27,
  input  in_28,
  input  in_29,
  input  in_30,
  input  in_31,
  input  in_32,
  input  [1:0] in_33,
  input  in_34,
  input  in_35,
  input  in_36,
  input  [1:0] in_37
);

  wire demultiplexer_1_out0, demultiplexer_1_out1, demultiplexer_1_out2, demultiplexer_1_out3,
       demultiplexer_2_out0, demultiplexer_2_out1, demultiplexer_2_out2, demultiplexer_3_out0,
       demultiplexer_3_out1, demultiplexer_3_out2, demultiplexer_3_out3, multiplexer_1_out,
       multiplexer_2_out, multiplexer_3_out, multiplexer_4_out, multiplexer_5_out;

  Multiplexer #(.select(2)) multiplexer_1 (
    .in0(in_4), .in1(in_2), .in2(in_3), .in3(in_1), .out(multiplexer_1_out), .sel(in_7), .en(in_8));
  Multiplexer #(.select(2)) multiplexer_2 (
    .in0(in_12), .in1(in_10), .in2(in_11), .in3(in_9), .out(multiplexer_2_out), .sel(in_15), .en(in_16));
  Demultiplexer #(.select(2)) demultiplexer_1 (
    .out0(demultiplexer_1_out0), .out1(demultiplexer_1_out1), .out2(demultiplexer_1_out2),
    .out3(demultiplexer_1_out3), .in(multiplexer_1_out), .sel(in_6), .en(in_5));
  Demultiplexer #(.select(2)) demultiplexer_2 (
    .out0(demultiplexer_2_out0), .out1(demultiplexer_2_out1), .out2(demultiplexer_2_out2),
    .in(multiplexer_2_out), .sel(in_14), .en(in_13));  // open: out3
  Demultiplexer #(.select(2)) demultiplexer_3 (
    .out0(demultiplexer_3_out0), .out1(demultiplexer_3_out1), .out2(demultiplexer_3_out2),
    .out3(demultiplexer_3_out3), .in(in_35), .sel(in_37), .en(in_36));
  _7_Segment_Display u_7_segment_display_1 (
    .g(demultiplexer_1_out3), .f(demultiplexer_1_out2), .a(demultiplexer_1_out1), .b(demultiplexer_1_out0),
    .e(demultiplexer_2_out0), .d(demultiplexer_2_out1), .c(demultiplexer_2_out2));  // open: dp
  Multiplexer #(.select(2)) multiplexer_3 (
    .in0(in_23), .in1(in_24), .in2(in_25), .in3(in_26), .out(multiplexer_3_out), .sel(in_27), .en(in_28));
  Multiplexer #(.select(2)) multiplexer_4 (
    .in0(in_29), .in1(in_30), .in2(in_31), .in3(in_32), .out(multiplexer_4_out), .sel(in_33), .en(in_34));
  _7_Segment_Display u_7_segment_display_2 (
    .g(demultiplexer_3_out3), .f(demultiplexer_3_out2), .a(demultiplexer_3_out1), .b(demultiplexer_3_out0));  // open: e, d, c, dp
  Multiplexer #(.select(2)) multiplexer_5 (
    .in0(in_17), .in1(in_18), .in2(in_19), .in3(in_20), .out(multiplexer_5_out), .sel(in_21), .en(in_22));
  _7_Segment_Display u_7_segment_display_3 (
    .a(multiplexer_3_out), .b(multiplexer_5_out), .c(multiplexer_4_out));  // open: g, f, e, d, dp
endmodule
