// Logisim project TENTATIVA DISPLAY 7 SEGMENTOS.circ as structural Verilog: 1 circuit, main circuit main
module main (
  input  in_1,
  input  [3:0] in_2
);

  wire demultiplexer_1_out0, multiplexer_1_out, undriven, undriven_2, undriven_3, undriven_4;

  Multiplexer #(.select(4), .enable("false")) multiplexer_1 (
    .in0(1'b1), .in1(1'b1), .in2(1'b1), .in3(1'b1), .in4(1'b1), .in5(1'b1), .in6(1'b1), .in7(1'b1),
    .in8(1'b1), .in9(1'b1), .out(multiplexer_1_out), .sel(in_2));  // open: in10, in11, in12, in13, in14, in15
  Demultiplexer #(.enable("false")) demultiplexer_1 (
    .out0(demultiplexer_1_out0), .in(multiplexer_1_out), .sel(in_1));  // open: out1
  _7_Segment_Display u_7_segment_display_1 (
    .g(undriven_3), .f(undriven_2), .a(demultiplexer_1_out0), .b(undriven), .e(undriven_4), .d(undriven_4),
    .c(undriven_4), .dp(undriven_4));
endmodule
