// Logisim project EXERCÍCIOS DA AULA 09 DIA 15.circ as structural Verilog: 2 circuits, main circuit main
module main (
  input  in_1,
  input  in_2,
  input  in_3,
  input  in_4,
  input  in_5,
  input  in_6,
  input  in_7,
  input  in_8,
  output out_9,
  output out_10,
  output out_11,
  output out_12,
  output out_13,
  output out_14
);

  wire and_1_out, and_2_out, and_3_out, and_4_out, and_5_out, button_1_out, d_ff_1_q, not_1_out, not_2_out;

  not not_1 (not_1_out, in_6);
  nand nand_1 (out_9, in_1, out_10);
  nand nand_2 (out_10, out_9, in_2);
  and and_1 (and_1_out, in_3, in_4);
  and and_2 (and_2_out, in_4, in_5);
  and and_3 (and_3_out, not_1_out, in_8);
  LED led_1 (.in(out_9));
  LED led_2 (.in(out_10));
  and and_4 (and_4_out, in_6, in_7);
  and and_5 (and_5_out, in_7, and_3_out);
  Button button_1 (.out(button_1_out));
  nor nor_1 (out_11, and_1_out, out_12);
  nor nor_2 (out_12, out_11, and_2_out);
  LED led_3 (.in(out_11));
  LED led_4 (.in(out_12));
  nor nor_3 (out_13, and_4_out, out_14);
  nor nor_4 (out_14, out_13, and_5_out);
  not not_2 (not_2_out, d_ff_1_q);
  D_Flip_Flop d_ff_1 (.clk(button_1_out), .D(not_2_out), .Q(d_ff_1_q));  // open: Qn, preset, en, reset
  LED led_5 (.in(out_13));
  LED led_6 (.in(out_14));
  LED led_7 (.in(d_ff_1_q));
  Button button_2 ();  // open: out
endmodule

module CIRCUITO_01 (
  input  in_1,
  input  in_2,
  output out_3,
  output out_4
);

  nand nand_1 (out_3, in_1, out_4);
  nand nand_2 (out_4, out_3, in_2);
  LED led_1 (.in(out_3));
  LED led_2 (.in(out_4));
endmodule
